// Digital circuit project.dig as structural Verilog
module project (
  input  Door_Open_Status,
  input  Secure_Mode,
  input  Daylight_Sensor,
  input  Weather_Sensor,
  input  [7:0] Temperature_Sensor_1,
  input  [7:0] Temperature_Sensor_2,
  input  [3:0] Water_Level_A,
  input  Max_Tank_B,
  input  Window1,
  input  Window2,
  input  Window3,
  input  Door_Lock_Status,
  output [2:0] out_13
);

  wire u_smart_house_electrovalve, u_smart_house_security_alert, u_smart_house_water_pump,
       u_smart_house_window_door_open_rain_alert, u_smart_house_window_open_at_night_alert,
       u_smart_house_window_open_security_mode;

  smart_house #(.applicationType("GHDL"), .CodeFile("\\home\\aluno\\Documentos\\bs\\CC-UFFS\\third-semester\\DIGITALSYSTEMS\\assignment1\\main.vhdl")) u_smart_house (
    .status_window({Window3, Window2, Window1}), .status_door({Door_Lock_Status, Door_Open_Status}),
    .secure_mode(Secure_Mode), .daylight_sensor(Daylight_Sensor), .weather_sensor(Weather_Sensor),
    .temperature_sensor_1(Temperature_Sensor_1), .temperature_sensor_2(Temperature_Sensor_2),
    .level_tankA(Water_Level_A), .max_tankB(Max_Tank_B), .security_alert(u_smart_house_security_alert),
    .window_open_warning(out_13), .window_open_security_mode(u_smart_house_window_open_security_mode),
    .window_open_at_night_alert(u_smart_house_window_open_at_night_alert),
    .window_door_open_rain_alert(u_smart_house_window_door_open_rain_alert),
    .water_pump(u_smart_house_water_pump), .electrovalve(u_smart_house_electrovalve));
  LED led_1 (.in(u_smart_house_security_alert));
  LED led_2 (.in(u_smart_house_window_open_security_mode));
  LED led_3 (.in(u_smart_house_window_open_at_night_alert));
  LED led_4 (.in(u_smart_house_window_door_open_rain_alert));
  LED led_5 (.in(u_smart_house_water_pump));
  LED led_6 (.in(u_smart_house_electrovalve));
endmodule
