// Digital circuit adder.dig as structural Verilog
module adder (
  input  [1:0] a,
  input  [1:0] b,
  input  flag,
  input  [1:0] a_2,
  input  [1:0] b_2,
  input  flag_2,
  output [1:0] sum,
  output carry,
  output [1:0] sum0,
  output carry_2
);

  wire u_full_adder_carry_out;

  four_bit_adder #(.applicationType("GHDL"), .CodeFile("/home/aluno/Documentos/bs/CC-UFFS/third-semester/DIGITALSYSTEMS/VHDL/adder/adder.vhdl")) u_four_bit_adder (
    .a(a), .b(b), .k(flag), .carry(carry), .sum(sum));
  full_adder #(.applicationType("GHDL"), .CodeFile("/home/aluno/Documentos/bs/CC-UFFS/third-semester/DIGITALSYSTEMS/VHDL/adder/adder.vhdl")) u_full_adder (
    .a(a_2[0]), .b(b_2[0]), .carry_in(flag_2), .carry_out(u_full_adder_carry_out), .sum(sum0[0]));
  full_adder #(.applicationType("GHDL"), .CodeFile("/home/aluno/Documentos/bs/CC-UFFS/third-semester/DIGITALSYSTEMS/VHDL/adder/adder.vhdl")) u_full_adder_2 (
    .a(a_2[1]), .b(b_2[1]), .carry_in(u_full_adder_carry_out), .carry_out(carry_2), .sum(sum0[1]));
endmodule
