// Digital circuit circuit.dig as structural Verilog
module circuit (
  input  in_2,
  input  in_3,
  input  in_4,
  input  in_5,
  input  in_8,
  input  in_9,
  input  in_10,
  input  in_11,
  output out_1,
  output out_6,
  output out_7,
  output out_12
);

  mux1 #(.applicationType("GHDL"), .CodeFile("/home/aluno/Documentos/bs/VHDL/mux1.vhd")) u_mux1 (
    .a(in_8), .b(in_3), .k(in_4), .s(out_1));
  dmux1 #(.applicationType("GHDL"), .CodeFile("/home/aluno/Documentos/bs/VHDL/dmux1.vhd")) u_dmux1 (
    .a(in_2), .k(in_5), .s1(out_6), .s2(out_7));
  ex1 #(.applicationType("GHDL"), .CodeFile("/home/aluno/Documentos/bs/VHDL/ex1.vhd")) u_ex1 (
    .a(in_9), .b(in_10), .c(in_11), .s(out_12));
endmodule
