// Digital circuit project.dig as structural Verilog
module project (
  input  [2:0] Status_Window,
  input  [1:0] Status_Door,
  input  Secure_Mode,
  input  Daylight_Sensor,
  input  Weather_Sensor,
  input  [7:0] Temperature_Sensor_1,
  input  [7:0] Temperature_Sensor_2,
  input  [3:0] Water_Level_A,
  input  Max_Tank_B,
  output [2:0] out_10
);

  wire u_smart_house_eletrovalve, u_smart_house_security_alert, u_smart_house_water_pump,
       u_smart_house_wdopen_rain_alert, u_smart_house_wopen_lowtemp_alert, u_smart_house_wopen_night_alert;

  smart_house #(.applicationType("GHDL"), .CodeFile("/home/aluno/Documentos/bs/CC-UFFS/third-semester/DIGITALSYSTEMS/assignment1/main.vhdl")) u_smart_house (
    .status_window(Status_Window), .status_door(Status_Door), .secure_mode(Secure_Mode),
    .daylight_sensor(Daylight_Sensor), .weather_sensor(Weather_Sensor),
    .temperature_sensor_1(Temperature_Sensor_1), .temperature_sensor_2(Temperature_Sensor_2),
    .level_tankA(Water_Level_A), .max_tankB(Max_Tank_B), .security_alert(u_smart_house_security_alert),
    .wdopen_alert(out_10), .wdopen_rain_alert(u_smart_house_wdopen_rain_alert),
    .wopen_night_alert(u_smart_house_wopen_night_alert),
    .wopen_lowtemp_alert(u_smart_house_wopen_lowtemp_alert), .water_pump(u_smart_house_water_pump),
    .eletrovalve(u_smart_house_eletrovalve));
  LED led_1 (.in(u_smart_house_security_alert));
  LED led_2 (.in(u_smart_house_wdopen_rain_alert));
  LED led_3 (.in(u_smart_house_wopen_night_alert));
  LED led_4 (.in(u_smart_house_wopen_lowtemp_alert));
  LED led_5 (.in(u_smart_house_water_pump));
  LED led_6 (.in(u_smart_house_eletrovalve));
endmodule
