// Digital circuit elevatorcircuit.dig as structural Verilog
module elevatorcircuit (
  input  in_1,
  input  in_2,
  input  in_3,
  input  in_4,
  input  in_5,
  input  in_6
);

  wire u_elevator_door_state;
  wire [3:0] u_elevator_floor_out;

  elevator #(.applicationType("GHDL"), .CodeFile("/home/aluno/Documentos/bs/CC-UFFS/third-semester/DIGITALSYSTEMS/assignment2/elevator.vhdl")) u_elevator (
    .CLK(in_1), .RST(in_2), .floor_btn({in_3, in_4, in_5, in_6}), .floor_out(u_elevator_floor_out),
    .door_state(u_elevator_door_state));
  LED led_1 (.in(u_elevator_floor_out[3]));
  LED led_2 (.in(u_elevator_floor_out[2]));
  LED led_3 (.in(u_elevator_floor_out[1]));
  LED led_4 (.in(u_elevator_floor_out[0]));
  LED led_5 (.in(u_elevator_door_state));
endmodule
